# Fritzing sketch circuit (saved by Fritzing 0.9.10b)

parts:
  U1 = ESP8266 NodeMCU LoLin module
  M2 = Dagu DGServo 9g (Top view) [part_number=RS001B]

nets:
  N1: U1.D2, M2.pulse
  GND: U1.GND, M2.gnd

custom parts:
  ESP8266 NodeMCU LoLin module: ESP8266 based NodeMCU
